// Logisim project jk_ff.circ as structural Verilog: 1 circuit, main circuit jk_ff
module jk_ff (
  input  j,
  input  k,
  input  clk,
  output q
);

  wire jt, kt, m, m_nd, m_r, m_s, mn, nc, next_d, nk, qn, s_nd, s_r, s_s;

  nand u_nc (nc, clk, clk);
  nand u_nk (nk, k, k);
  nand u_jt (jt, j, qn);
  nand u_kt (kt, nk, q);
  nand u_next_d (next_d, jt, kt);
  nand u_m_s (m_s, next_d, nc);
  nand u_m_nd (m_nd, next_d, next_d);
  nand u_m_r (m_r, m_nd, nc);
  nand u_m (m, m_s, mn);
  nand u_mn (mn, m_r, m);
  nand u_s_s (s_s, m, clk);
  nand u_s_nd (s_nd, m, m);
  nand u_s_r (s_r, s_nd, clk);
  nand u_q (q, s_s, qn);
  nand u_qn (qn, s_r, q);
endmodule
